// Logisim project 4BitBinaryToDeneryConverter.circ as structural Verilog: 1 circuit, main circuit main
module main (
  input  in_1,
  input  in_2,
  input  in_3,
  input  in_4
);

  wire and_1_out, and_2_out, and_3_out, and_4_out, and_5_out, and_6_out, and_7_out, and_8_out, and_9_out,
       and_10_out, and_11_out, and_12_out, and_13_out, and_14_out, and_15_out, and_16_out, not_1_out,
       not_2_out, not_3_out, not_4_out, not_5_out, not_6_out, not_7_out, not_8_out, not_9_out, not_10_out,
       not_11_out, not_12_out, not_13_out, not_14_out, not_15_out, not_16_out, not_17_out, not_18_out,
       not_19_out, not_20_out, not_21_out, not_22_out, not_23_out, not_24_out, not_25_out, not_26_out,
       not_27_out, not_28_out, not_29_out, not_30_out, not_31_out, not_32_out, or_1_out, or_2_out, or_3_out,
       or_4_out, or_5_out, or_6_out, or_7_out, or_8_out, or_9_out, or_10_out, or_11_out, or_12_out,
       or_13_out, or_14_out, or_15_out, or_16_out, or_17_out, or_18_out, or_19_out, or_20_out, or_21_out,
       or_22_out, or_23_out, or_24_out, or_25_out, or_26_out, or_27_out, or_28_out, or_29_out, or_30_out,
       or_31_out, or_32_out, or_33_out, or_34_out, or_35_out, or_36_out;

  or or_1 (or_1_out, and_2_out, and_1_out, and_3_out, and_4_out, and_5_out);
  not not_1 (not_1_out, in_4);
  or or_2 (or_2_out, and_6_out, and_7_out, and_8_out, and_9_out, and_10_out);
  and and_1 (and_1_out, in_4, not_2_out, not_6_out, not_10_out);
  and and_2 (and_2_out, not_1_out, not_5_out, not_4_out, not_3_out);
  not not_2 (not_2_out, in_3);
  not not_3 (not_3_out, in_1);
  not not_4 (not_4_out, in_2);
  not not_5 (not_5_out, in_3);
  or or_3 (or_3_out, and_11_out, and_12_out, and_13_out, and_14_out, and_15_out);
  and and_3 (and_3_out, not_8_out, in_3, not_7_out, not_9_out);
  not not_6 (not_6_out, in_2);
  not not_7 (not_7_out, in_2);
  not not_8 (not_8_out, in_4);
  not not_9 (not_9_out, in_1);
  not not_10 (not_10_out, in_1);
  and and_4 (and_4_out, in_4, in_3, not_12_out, not_11_out);
  not not_11 (not_11_out, in_1);
  not not_12 (not_12_out, in_2);
  not not_13 (not_13_out, in_4);
  or or_4 (or_4_out, or_1_out, or_2_out);
  or or_5 (or_5_out, or_3_out, and_16_out);
  and and_5 (and_5_out, not_13_out, not_14_out, in_2, not_15_out);
  and and_6 (and_6_out, in_4, not_16_out, in_2, not_17_out);
  not not_14 (not_14_out, in_3);
  not not_15 (not_15_out, in_1);
  not not_16 (not_16_out, in_3);
  and and_7 (and_7_out, not_19_out, in_3, in_2, not_18_out);
  not not_17 (not_17_out, in_1);
  not not_18 (not_18_out, in_1);
  not not_19 (not_19_out, in_4);
  and and_8 (and_8_out, in_4, in_3, in_2, not_21_out);
  not not_20 (not_20_out, in_4);
  not not_21 (not_21_out, in_1);
  or or_6 (or_6_out, or_4_out, or_5_out);
  buf or_7 (or_7_out, or_4_out);  // OR_Gate
  buf or_8 (or_8_out, or_4_out);  // OR_Gate
  // OR_Gate or_9 has open pins: out=or_9_out
  _7_Segment_Display u_7_segment_display_1 (
    .g(or_9_out), .f(or_8_out), .a(or_7_out), .b(or_6_out), .e(or_10_out), .d(or_11_out), .c(or_12_out));  // open: dp
  buf or_10 (or_10_out, or_4_out);  // OR_Gate
  buf or_11 (or_11_out, or_4_out);  // OR_Gate
  or or_12 (or_12_out, or_4_out, or_5_out);
  and and_9 (and_9_out, not_20_out, not_23_out, not_24_out, in_1);
  and and_10 (and_10_out, in_4, not_22_out, not_25_out, in_1);
  not not_22 (not_22_out, in_3);
  not not_23 (not_23_out, in_3);
  not not_24 (not_24_out, in_2);
  and and_11 (and_11_out, not_27_out, in_3, not_26_out, in_1);
  not not_25 (not_25_out, in_2);
  not not_26 (not_26_out, in_2);
  not not_27 (not_27_out, in_4);
  and and_12 (and_12_out, in_4, in_3, not_28_out, in_1);
  not not_28 (not_28_out, in_2);
  not not_29 (not_29_out, in_4);
  buf or_13 (or_13_out, and_7_out);  // OR_Gate
  buf or_14 (or_14_out, and_8_out);  // OR_Gate
  buf or_15 (or_15_out, and_9_out);  // OR_Gate
  buf or_16 (or_16_out, and_10_out);  // OR_Gate
  and and_13 (and_13_out, not_29_out, not_31_out, in_2, in_1);
  and and_14 (and_14_out, in_4, not_30_out, in_2, in_1);
  not not_30 (not_30_out, in_3);
  not not_31 (not_31_out, in_3);
  or or_17 (or_17_out, and_2_out, and_11_out);
  or or_18 (or_18_out, and_1_out, and_12_out);
  or or_19 (or_19_out, and_3_out, and_13_out);
  or or_20 (or_20_out, and_4_out, and_14_out);
  or or_21 (or_21_out, and_5_out, and_15_out);
  or or_22 (or_22_out, and_6_out, and_16_out);
  or or_23 (or_23_out, or_14_out, or_28_out);
  and and_15 (and_15_out, not_32_out, in_3, in_2, in_1);
  not not_32 (not_32_out, in_4);
  or or_24 (or_24_out, or_23_out, or_21_out);
  or or_25 (or_25_out, or_27_out, or_23_out);
  or or_26 (or_26_out, or_28_out, or_27_out);
  or or_27 (or_27_out, or_22_out, or_13_out);
  or or_28 (or_28_out, or_15_out, or_16_out);
  and and_16 (and_16_out, in_4, in_3, in_2, in_1);
  or or_29 (or_29_out, or_27_out, or_23_out);
  or or_30 (or_30_out, or_17_out, or_18_out, or_19_out, or_20_out, or_24_out);
  or or_31 (or_31_out, or_17_out, or_19_out, or_20_out, or_25_out);
  or or_32 (or_32_out, or_17_out, or_21_out, or_27_out, or_28_out);
  or or_33 (or_33_out, or_19_out, or_20_out, or_21_out, or_26_out);
  or or_34 (or_34_out, or_17_out, or_19_out, or_15_out, or_13_out);
  or or_35 (or_35_out, or_17_out, or_19_out, or_20_out, or_27_out, or_28_out);
  or or_36 (or_36_out, or_17_out, or_18_out, or_20_out, or_21_out, or_29_out);
  _7_Segment_Display u_7_segment_display_2 (
    .g(or_33_out), .f(or_32_out), .a(or_31_out), .b(or_30_out), .e(or_34_out), .d(or_35_out), .c(or_36_out));  // open: dp
endmodule
